# Fritzing sketch Analog (saved by Fritzing 0.9.2b)
circuit board: 8.46667cm x 5.64444cm
breadboards: 1

parts:
  LED2 = LED - 3mm [color="Red (633nm)" package="3 mm [THT]"]
  IC5 = DIP - 18 pins [chip_label="REEPSUB V1.1" package="DIP (Dual Inline) [THT]"]
  R2 = Resistor [tolerance=±0.1% resistance=10k package=THT]
  R3 = PHOTOCELL [package=photocell-kit]
  R1 = Resistor [tolerance=±10% resistance=1k package="2010 [SMD]"]

nets:
  N1: LED2.cathode, IC5.GND#17, R1.Pin_1
  N2: LED2.anode, IC5.IO15
  N3: IC5.TOUT, R2.Pin_1, R1.Pin_0
  N4: IC5.3V3, R3.P$1
  N5: R2.Pin_0, R3.P$2

notes:
  get analog sensor value

custom parts:
  DIP - 18 pins: A DIP stand-in part for whatever IC you want. With 18 pins on a 900mil dual inline package (DIP) footprint.
