# Fritzing sketch 回路図A (saved by Fritzing 0.9.2b)
circuit board: 8.46667cm x 5.64444cm
breadboards: 1

parts:
  LED2 = LED - 3mm [color="Red (633nm)" package="3 mm [THT]"]
  LED1 = LED - 3mm [color="Green (555nm)" package="3 mm [THT]"]
  IC5 = DIP - 18 pins [chip_label="REEPSUB V1.1" package="DIP (Dual Inline) [THT]"]
  R1 = Resistor [tolerance=±10% resistance=260 package="2010 [SMD]"]
  R2 = Resistor [tolerance=±20% resistance=260 package=THT]

nets:
  N1: LED2.cathode, R2.Pin_1
  N2: LED2.anode, LED1.anode, IC5.GND#17
  N3: LED1.cathode, R1.Pin_1
  N4: IC5.IO12, R1.Pin_0
  N5: IC5.IO15, R2.Pin_0

custom parts:
  DIP - 18 pins: A DIP stand-in part for whatever IC you want. With 18 pins on a 900mil dual inline package (DIP) footprint.
