# Fritzing sketch 回路図Simple_1 (saved by Fritzing 0.9.2b)
circuit board: 8.46667cm x 5.64444cm
breadboards: 1

parts:
  LED2 = LED - 3mm [color="Red (633nm)" package="3 mm [THT]"]
  R1 = Resistor [tolerance=±10% resistance=260 package="2010 [SMD]"]
  VCC1 = Battery
  LED1 = LED - 3mm [color="Green (555nm)" package="3 mm [THT]"]  # not connected

nets:
  N1: LED2.cathode, VCC1.-
  N2: LED2.anode, R1.Pin_0
  N3: R1.Pin_1, VCC1.+
