# Fritzing sketch 回路図Simple_5 (saved by Fritzing 0.9.2b)
circuit board: 8.46667cm x 5.64444cm
breadboards: 1

parts:
  LED2 = LED - 3mm [color="Red (633nm)" package="3 mm [THT]"]
  R1 = Resistor [tolerance=±10% resistance=260 package="2010 [SMD]"]  # not connected
  VCC1 = Battery
  LED1 = LED - 3mm [color="Green (555nm)" package="3 mm [THT]"]  # not connected
  S1 = Toggle Switch [package=THT]  # not connected
  S2 = Reed switch [package=THT]  # not connected
  S3 = SWITCH-MOMENTARY-2 [package=tactile-switch-1101ne]  # not connected
  S4 = SPST Switch [package=switch-spdt_lock.007s]  # not connected
  U2 = TMP36 [package=to-92]
  R4 = Resistor [tolerance=±10% resistance=10k package="2010 [SMD]"]

nets:
  N1: LED2.cathode, VCC1.-, U2.VCC, R4.Pin_1
  N2: LED2.anode, U2.VOUT, R4.Pin_0
  N3: VCC1.+, U2.GND

notes:
  コレで動かした後、スイッチ、光センサに変えて動作を確認する。
